// Logisim project PandesalCPU.circ as structural Verilog: 18 circuits, main circuit PandesalCPU
module PandesalCPU (
  input  Reset
);

  wire ABL_cout, clock_1_out, decoder_1_out0, decoder_1_out1, decoder_1_out2, decoder_1_out3, decoder_1_out4,
       decoder_1_out6, decoder_1_out7, decoder_1_out8, decoder_1_out9, decoder_1_out10, decoder_1_out11,
       decoder_1_out12, decoder_1_out13, decoder_1_out14, decoder_1_out15, decoder_2_out0, decoder_2_out1,
       decoder_2_out2, decoder_2_out3, decoder_2_out4, decoder_2_out5, decoder_2_out6, decoder_2_out7,
       decoder_2_out8, decoder_2_out9, decoder_2_out10, decoder_2_out11, decoder_2_out12, decoder_2_out13,
       decoder_2_out14, decoder_2_out15, demultiplexer_1_out0, demultiplexer_1_out1, demultiplexer_2_out0,
       demultiplexer_2_out1, demultiplexer_3_out0, demultiplexer_3_out1, multiplexer_1_out,
       multiplexer_2_out, not_1_out, not_2_out, not_3_out, not_4_out, or_1_out, PCL_c;
  wire [1:0] multiplexer_3_out;
  wire [3:0] ALU_n, multiplexer_4_out, S, StepCounter_o;
  wire [7:0] A, ABH, ABL, ALU_y, B, GP0, GP1, GP2, GP3, GP4, Instruction_Register_q, IR, O, PCH, PCL, SP, X,
       Y;
  wire [15:0] Microcode_data;

  Clock clock_1 (.out(clock_1_out));
  Register8 Instruction_Register (
    .D(Instruction_Register_q), .Load(decoder_1_out2), .Enable(decoder_2_out2), .Clk(clock_1_out),
    .Reset(Reset), .Q(Instruction_Register_q), .AlwaysQ(IR));
  ROM #(.addrWidth(12), .dataWidth(16)) Microcode (.addr({IR, StepCounter_o}), .data(Microcode_data));
  // Probe on B
  Increment4 StepCounter (.Reset(or_1_out), .Clk(clock_1_out), .O(StepCounter_o));
  or or_1 (or_1_out, Reset, multiplexer_1_out, Microcode_data[1]);
  Multiplexer multiplexer_1 (.in0(1'b0), .in1(multiplexer_2_out), .out(multiplexer_1_out), .sel(Microcode_data[2]));
  not not_1 (not_1_out, S[3]);
  not not_2 (not_2_out, S[2]);
  not not_3 (not_3_out, S[0]);
  Multiplexer #(.select(3)) multiplexer_2 (
    .in0(S[3]), .in1(not_1_out), .in2(not_2_out), .in3(not_3_out), .in4(S[2]), .in5(S[0]), .in6(S[1]),
    .in7(not_4_out), .out(multiplexer_2_out));  // open: sel
  not not_4 (not_4_out, S[1]);
  // Probe on {ABH[6:0], ABL}
  RAM #(.addrWidth(15), .databus("bidir"), .trigger("high"), .\type ("nonvolatile")) ram_1 (
    .addr({ABH[6:0], ABL}), .we(decoder_1_out15), .oe(decoder_2_out15), .data(Instruction_Register_q));
  // Probe on {ABH[6:0], ABL}
  // Probe on A
  // Probe on A
  // Probe on SP
  Multiplexer #(.width(2)) multiplexer_3 (
    .in0({1'b0, Microcode_data[0]}), .in1(2'b10), .out(multiplexer_3_out), .sel(Microcode_data[2]));
  Demultiplexer demultiplexer_1 (
    .out0(demultiplexer_1_out0), .out1(demultiplexer_1_out1), .in(decoder_2_out0), .sel(Microcode_data[3]));
  Decoder #(.enable("false"), .select(4)) decoder_1 (
    .out0(decoder_1_out0), .out1(decoder_1_out1), .out2(decoder_1_out2), .out3(decoder_1_out3),
    .out4(decoder_1_out4), .out6(decoder_1_out6), .out7(decoder_1_out7), .out8(decoder_1_out8),
    .out9(decoder_1_out9), .out10(decoder_1_out10), .out11(decoder_1_out11), .out12(decoder_1_out12),
    .out13(decoder_1_out13), .out14(decoder_1_out14), .out15(decoder_1_out15), .sel(Microcode_data[11:8]));  // open: out5
  Decoder #(.enable("false"), .select(4)) decoder_2 (
    .out0(decoder_2_out0), .out1(decoder_2_out1), .out2(decoder_2_out2), .out3(decoder_2_out3),
    .out4(decoder_2_out4), .out5(decoder_2_out5), .out6(decoder_2_out6), .out7(decoder_2_out7),
    .out8(decoder_2_out8), .out9(decoder_2_out9), .out10(decoder_2_out10), .out11(decoder_2_out11),
    .out12(decoder_2_out12), .out13(decoder_2_out13), .out14(decoder_2_out14), .out15(decoder_2_out15),
    .sel(Microcode_data[15:12]));
  Demultiplexer demultiplexer_2 (
    .out0(demultiplexer_2_out0), .out1(demultiplexer_2_out1), .in(decoder_1_out0), .sel(Microcode_data[3]));
  Demultiplexer demultiplexer_3 (
    .out0(demultiplexer_3_out0), .out1(demultiplexer_3_out1), .in(decoder_1_out1), .sel(Microcode_data[3]));
  assign Instruction_Register_q[0] = decoder_2_out1 ? decoder_2_out1 : 1'bz;  // Controlled_Buffer controlled_buffer_1
  assign Instruction_Register_q[1] = decoder_2_out1 ? 1'b0 : 1'bz;  // Controlled_Buffer controlled_buffer_2
  assign Instruction_Register_q[2] = decoder_2_out1 ? 1'b0 : 1'bz;  // Controlled_Buffer controlled_buffer_3
  assign Instruction_Register_q[3] = decoder_2_out1 ? 1'b0 : 1'bz;  // Controlled_Buffer controlled_buffer_4
  assign Instruction_Register_q[4] = decoder_2_out1 ? 1'b0 : 1'bz;  // Controlled_Buffer controlled_buffer_5
  assign Instruction_Register_q[5] = decoder_2_out1 ? 1'b0 : 1'bz;  // Controlled_Buffer controlled_buffer_6
  assign Instruction_Register_q[6] = decoder_2_out1 ? 1'b0 : 1'bz;  // Controlled_Buffer controlled_buffer_7
  assign Instruction_Register_q[7] = decoder_2_out1 ? 1'b0 : 1'bz;  // Controlled_Buffer controlled_buffer_8
  Hex_Digit_Display #(.decimalPoint("false")) hex_digit_display_1 (.value(PCH[7:4]));
  Hex_Digit_Display #(.decimalPoint("false")) hex_digit_display_2 (.value(PCH[3:0]));
  _7_Segment_Display #(.decimalPoint("false")) u_7_segment_display_1 (.b(S[3]), .c(S[3]));  // open: g, f, a, e, d
  _7_Segment_Display #(.decimalPoint("false")) u_7_segment_display_2 (.b(S[2]), .c(S[2]));  // open: g, f, a, e, d
  Hex_Digit_Display #(.decimalPoint("false")) hex_digit_display_3 (.value(X[7:4]));
  Hex_Digit_Display #(.decimalPoint("false")) hex_digit_display_4 (.value(GP2[7:4]));
  Hex_Digit_Display #(.decimalPoint("false")) hex_digit_display_5 (.value(PCL[7:4]));
  Hex_Digit_Display #(.decimalPoint("false")) hex_digit_display_6 (.value(PCL[3:0]));
  _7_Segment_Display #(.decimalPoint("false")) u_7_segment_display_3 (.b(S[1]), .c(S[1]));  // open: g, f, a, e, d
  _7_Segment_Display #(.decimalPoint("false")) u_7_segment_display_4 (.b(S[0]), .c(S[0]));  // open: g, f, a, e, d
  Hex_Digit_Display #(.decimalPoint("false")) hex_digit_display_7 (.value(X[3:0]));
  Hex_Digit_Display #(.decimalPoint("false")) hex_digit_display_8 (.value(GP2[3:0]));
  Hex_Digit_Display #(.decimalPoint("false")) hex_digit_display_9 (.value(ABH[7:4]));
  ProgramCounter u_PCL (
    .Cin(1'b0), .Inc(multiplexer_3_out), .Load(demultiplexer_2_out0), .Reset(Reset), .Clk(clock_1_out),
    .Address(Instruction_Register_q), .Enable(demultiplexer_1_out0), .C(PCL_c), .PC(Instruction_Register_q),
    .AlwaysQ(PCL));
  ProgramCounter u_PCH (
    .Cin(PCL_c), .Inc(2'b00), .Load(demultiplexer_2_out1), .Reset(Reset), .Clk(clock_1_out),
    .Address(Instruction_Register_q), .Enable(demultiplexer_1_out1), .PC(Instruction_Register_q),
    .AlwaysQ(PCH));  // open: C
  Register8 GP_Register1 (
    .D(Instruction_Register_q), .Load(decoder_1_out11), .Enable(decoder_2_out11), .Clk(clock_1_out),
    .Reset(Reset), .Q(Instruction_Register_q), .AlwaysQ(GP1));
  Register8 GP_Register2 (
    .D(Instruction_Register_q), .Load(decoder_1_out12), .Enable(decoder_2_out12), .Clk(clock_1_out),
    .Reset(Reset), .Q(Instruction_Register_q), .AlwaysQ(GP2));
  Register8 GP_Register3 (
    .D(Instruction_Register_q), .Load(decoder_1_out13), .Enable(decoder_2_out13), .Clk(clock_1_out),
    .Reset(Reset), .Q(Instruction_Register_q), .AlwaysQ(GP3));
  Register8 GP_Register4 (
    .D(Instruction_Register_q), .Load(decoder_1_out14), .Enable(decoder_2_out14), .Clk(clock_1_out),
    .Reset(Reset), .Q(Instruction_Register_q), .AlwaysQ(GP4));
  Hex_Digit_Display #(.decimalPoint("false")) hex_digit_display_10 (.value(ABH[3:0]));
  Hex_Digit_Display #(.decimalPoint("false")) hex_digit_display_11 (.value(ABL[7:4]));
  Hex_Digit_Display #(.decimalPoint("false")) hex_digit_display_12 (.value(O[7:4]));
  Hex_Digit_Display #(.decimalPoint("false")) hex_digit_display_13 (.value(O[3:0]));
  Hex_Digit_Display #(.decimalPoint("false")) hex_digit_display_14 (.value(Y[7:4]));
  Hex_Digit_Display #(.decimalPoint("false")) hex_digit_display_15 (.value(Y[3:0]));
  Hex_Digit_Display #(.decimalPoint("false")) hex_digit_display_16 (.value(GP3[7:4]));
  Hex_Digit_Display #(.decimalPoint("false")) hex_digit_display_17 (.value(GP3[3:0]));
  Hex_Digit_Display #(.decimalPoint("false")) hex_digit_display_18 (.value(ABL[3:0]));
  Hex_Digit_Display #(.decimalPoint("false")) hex_digit_display_19 (.value(SP[7:4]));
  Hex_Digit_Display #(.decimalPoint("false")) hex_digit_display_20 (.value(A[7:4]));
  Hex_Digit_Display #(.decimalPoint("false")) hex_digit_display_21 (.value(GP0[7:4]));
  Hex_Digit_Display #(.decimalPoint("false")) hex_digit_display_22 (.value(GP4[7:4]));
  Hex_Digit_Display #(.decimalPoint("false")) hex_digit_display_23 (.value(SP[3:0]));
  Hex_Digit_Display #(.decimalPoint("false")) hex_digit_display_24 (.value(A[3:0]));
  Hex_Digit_Display #(.decimalPoint("false")) hex_digit_display_25 (.value(GP0[3:0]));
  Hex_Digit_Display #(.decimalPoint("false")) hex_digit_display_26 (.value(GP4[3:0]));
  Register8 GP_Register0 (
    .D(Instruction_Register_q), .Load(decoder_1_out3), .Enable(decoder_2_out3), .Clk(clock_1_out),
    .Reset(Reset), .Q(Instruction_Register_q), .AlwaysQ(GP0));
  DataLatch8 ALU_out (
    .D(ALU_y), .Load(Microcode_data[4]), .Enable(decoder_2_out5), .Q(Instruction_Register_q), .AlwaysQ(O));
  ArithmeticLogicUnit ALU (
    .Opcode(Microcode_data[7:5]), .Cin(S[3]), .A(A), .B(B), .Ignore_Cin(Microcode_data[3]), .Y(ALU_y),
    .C(ALU_n[3]), .Z(ALU_n[2]), .O(ALU_n[1]), .N(ALU_n[0]));
  Register8 Accumulator (
    .D(Instruction_Register_q), .Load(decoder_1_out6), .Enable(decoder_2_out6), .Clk(clock_1_out),
    .Reset(Reset), .Q(Instruction_Register_q), .AlwaysQ(A));
  Register8 Y_Index (
    .D(Instruction_Register_q), .Load(decoder_1_out10), .Enable(decoder_2_out10), .Clk(clock_1_out),
    .Reset(Reset), .Q(Instruction_Register_q), .AlwaysQ(Y));
  Hex_Digit_Display #(.decimalPoint("false")) hex_digit_display_27 (.value(IR[7:4]));
  Hex_Digit_Display #(.decimalPoint("false")) hex_digit_display_28 (.value(IR[3:0]));
  Hex_Digit_Display #(.decimalPoint("false")) hex_digit_display_29 (.value(B[7:4]));
  Hex_Digit_Display #(.decimalPoint("false")) hex_digit_display_30 (.value(B[3:0]));
  Hex_Digit_Display #(.decimalPoint("false")) hex_digit_display_31 (.value(GP1[7:4]));
  Hex_Digit_Display #(.decimalPoint("false")) hex_digit_display_32 (.value(GP1[3:0]));
  StackRegister8 Stack_Pointer (
    .D(Instruction_Register_q), .Load(decoder_1_out8), .Enable(decoder_2_out8), .Clk(clock_1_out),
    .Reset(Reset), .Q(Instruction_Register_q), .AlwaysQ(SP));
  Register4 Status (
    .D(multiplexer_4_out), .Load(Microcode_data[4]), .Enable(decoder_2_out4), .Clk(clock_1_out),
    .Reset(Reset), .Q(Instruction_Register_q[3:0]), .AlwaysQ(S));
  Register8 X_Index (
    .D(Instruction_Register_q), .Load(decoder_1_out9), .Enable(decoder_2_out9), .Clk(clock_1_out),
    .Reset(Reset), .Q(Instruction_Register_q), .AlwaysQ(X));
  Register8 ALU_B (
    .D(Instruction_Register_q), .Load(decoder_1_out7), .Enable(decoder_2_out7), .Clk(clock_1_out),
    .Reset(Reset), .Q(Instruction_Register_q), .AlwaysQ(B));
  Multiplexer #(.width(4)) multiplexer_4 (
    .in0(ALU_n), .in1(Instruction_Register_q[3:0]), .out(multiplexer_4_out), .sel(decoder_1_out4));
  Address_Bus u_ABL (
    .Address(Instruction_Register_q), .Load(demultiplexer_3_out0), .Clk(clock_1_out), .Reset(Reset),
    .Cin(1'b0), .Inc(Microcode_data[0]), .O(ABL), .Cout(ABL_cout));
  Address_Bus u_ABH (
    .Address(Instruction_Register_q), .Load(demultiplexer_3_out1), .Clk(clock_1_out), .Reset(Reset),
    .Cin(ABL_cout), .Inc(1'b0), .O(ABH));  // open: Cout

  // Notes on the sheet:
  //   contents of Microcode (hex, n*v repeats v):
  //   100 108 f201 2 12*0 100 108 f201 f603 12*0 100 108 f201 f701 f108 7101 6f02 9*0 100 108 f201 f701
  //   f008 7002 10*0 100 108 f201 f700 5613 11*0 100 108 f201 f700 5673 11*0 100 108 f201 f700 56b3 11*0
  //   100 108 f201 f700 5693 11*0 100 108 f201 f700 5653 11*0 100 108 f201 f903 12*0 100 108 f201 fa03
  //   12*0 100 108 f201 6902 12*0 100 108 f201 6a02 12*0 100 108 f201 f701 f108 7100 9f02 9*0 100 108 f201
  //   f701 f108 7100 af02 9*0 100 108 f201 8902 12*0 100 108 f201 9602 12*0 100 108 f201 9802 12*0 100 108
  //   f201 a602 12*0 100 108 f201 f700 5633 11*0 100 108 f201 8100 1108 6f00 8600 1700 583a 7*0 100 108
  //   f201 8600 1700 5818 8100 1108 f602 7*0 100 108 f201 8100 1108 f08 8600 1700 5838 8100 0 f00 8638
  //   583a 0 0 100 108 f201 2700 4600 5472 26*0 100 108 f201 f701 f108 7100 f603 9*0 100 108 f201 f701
  //   f108 7100 f701 0 5612 7*0 100 108 f201 8600 1708 5818 8100 1108 f000 8608 5819 f00b 4*0 100 108 f201
  //   f701 f108 7100 f701 0 5632 7*0 100 108 f201 2700 4600 5472 10*0 100 108 f201 2204 f001 f00a 10*0 100
  //   108 f201 2224 f001 f00a 10*0 100 108 f201 2244 f001 f00a 10*0 100 108 f201 2264 f001 f00a 10*0 100
  //   108 f201 2284 f001 f00a 10*0 100 108 f201 22a4 f001 f00a 10*0 100 108 f201 22c4 f001 f00a 10*0 100
  //   108 f201 22e4 f001 f00a 10*0 100 108 f201 9600 1700 591a 10*0 100 108 f201 a600 1700 5a1a 10*0 100
  //   108 f201 2700 4600 54b2 10*0 100 108 f201 9600 1700 593a 10*0 100 108 f201 a600 1700 5a3a
  //   C
  //   Z
  //   Program Counter
  //   Status
  //   O
  //   N
  //   X Index
  //   General Purpose 2
  //   Address Bus
  //   ALU Out
  //   Y Index
  //   General Purpose 3
  //   Stack Pointer
  //   Accumulator
  //   14th term of the Fibonacci Sequence: 233
  //   0xE9 = 233
  //   General Purpose 0
  //   General Purpose 4
  //   Instruction
  //   ALU B
  //   General Purpose 1
endmodule

module ArithmeticLogicUnit (
  input  [2:0] Opcode,
  input  Cin,
  input  [7:0] A,
  input  [7:0] B,
  input  Ignore_Cin,
  output [7:0] Y,
  output C,
  output Z,
  output O,
  output N
);

  wire multiplexer_1_out, multiplexer_2_out, multiplexer_3_out, multiplexer_5_out, multiplexer_6_out,
       multiplexer_7_out, multiplexer_8_out, multiplexer_9_out, multiplexer_10_out, multiplexer_11_out,
       multiplexer_12_out, multiplexer_13_out, multiplexer_14_out, multiplexer_15_out, multiplexer_16_out,
       multiplexer_17_out, multiplexer_18_out, multiplexer_19_out, multiplexer_20_out, multiplexer_21_out,
       multiplexer_22_out, multiplexer_23_out, multiplexer_24_out, multiplexer_25_out, multiplexer_26_out,
       multiplexer_27_out, multiplexer_28_out, multiplexer_29_out, multiplexer_30_out, multiplexer_31_out,
       multiplexer_32_out, multiplexer_33_out, multiplexer_34_out, multiplexer_35_out, multiplexer_36_out,
       not_1_out, not_2_out, not_3_out, not_4_out, not_5_out, not_6_out, not_7_out, not_8_out, not_9_out,
       not_10_out, xor_1_out, xor_2_out;
  wire [7:0] and_2_out, cla8_1_sum, multiplexer_4_out, multiplexer_37_out, multiplexer_45_out,
       negate8_1_nega, not_11_out, or_1_out, xor_3_out;

  // Probe on A
  // Probe on A
  // Probe on A
  // Probe on B
  // Probe on B
  // Probe on B
  xor xor_1 (xor_1_out, A[7], B[7]);
  not not_1 (not_1_out, N);
  not not_2 (not_2_out, Y[6]);
  not not_3 (not_3_out, Y[5]);
  not not_4 (not_4_out, Y[4]);
  and and_1 (Z, not_1_out, not_2_out, not_3_out, not_4_out, not_6_out, not_7_out, not_8_out, not_9_out);
  not not_5 (not_5_out, xor_1_out);
  Multiplexer multiplexer_1 (.in0(not_5_out), .in1(xor_1_out), .out(multiplexer_1_out), .sel(Opcode[0]));
  not not_6 (not_6_out, Y[3]);
  not not_7 (not_7_out, Y[2]);
  not not_8 (not_8_out, Y[1]);
  not not_9 (not_9_out, Y[0]);
  and and_2 (and_2_out[0], A[0], B[0]);
  and and_3 (and_2_out[1], A[1], B[1]);
  and and_4 (and_2_out[2], A[2], B[2]);
  and and_5 (and_2_out[3], A[3], B[3]);
  and and_6 (and_2_out[4], A[4], B[4]);
  and and_7 (and_2_out[5], A[5], B[5]);
  and and_8 (and_2_out[6], A[6], B[6]);
  and and_9 (and_2_out[7], A[7], B[7]);
  or or_1 (or_1_out[0], A[0], B[0]);
  or or_2 (or_1_out[1], A[1], B[1]);
  or or_3 (or_1_out[2], A[2], B[2]);
  or or_4 (or_1_out[3], A[3], B[3]);
  or or_5 (or_1_out[4], A[4], B[4]);
  or or_6 (or_1_out[5], A[5], B[5]);
  or or_7 (or_1_out[6], A[6], B[6]);
  or or_8 (or_1_out[7], A[7], B[7]);
  xor xor_2 (xor_2_out, A[7], N);
  and and_10 (O, multiplexer_1_out, xor_2_out);
  Negate8 negate8_1 (.A(B), .NegA(negate8_1_nega));
  Multiplexer multiplexer_2 (.in0(Cin), .in1(not_10_out), .out(multiplexer_2_out), .sel(Opcode[0]));
  not not_10 (not_10_out, Cin);
  Multiplexer multiplexer_3 (.in0(multiplexer_2_out), .in1(1'b0), .out(multiplexer_3_out), .sel(Ignore_Cin));
  Multiplexer #(.width(8)) multiplexer_4 (.in0(B), .in1(negate8_1_nega), .out(multiplexer_4_out), .sel(Opcode[0]));
  Multiplexer multiplexer_5 (.in0(A[0]), .in1(A[4]), .out(multiplexer_5_out), .sel(B[2]));
  Multiplexer multiplexer_6 (.in0(A[1]), .in1(A[5]), .out(multiplexer_6_out), .sel(B[2]));
  Multiplexer multiplexer_7 (.in0(A[2]), .in1(A[6]), .out(multiplexer_7_out), .sel(B[2]));
  Multiplexer multiplexer_8 (.in0(A[3]), .in1(A[7]), .out(multiplexer_8_out), .sel(B[2]));
  Multiplexer multiplexer_9 (.in0(A[4]), .in1(1'b0), .out(multiplexer_9_out), .sel(B[2]));
  Multiplexer multiplexer_10 (.in0(A[5]), .in1(1'b0), .out(multiplexer_10_out), .sel(B[2]));
  Multiplexer multiplexer_11 (.in0(A[6]), .in1(1'b0), .out(multiplexer_11_out), .sel(B[2]));
  Multiplexer multiplexer_12 (.in0(A[7]), .in1(1'b0), .out(multiplexer_12_out), .sel(B[2]));
  Multiplexer multiplexer_13 (.in0(A[0]), .in1(1'b0), .out(multiplexer_13_out), .sel(B[2]));
  Multiplexer multiplexer_14 (.in0(A[1]), .in1(1'b0), .out(multiplexer_14_out), .sel(B[2]));
  Multiplexer multiplexer_15 (.in0(A[2]), .in1(1'b0), .out(multiplexer_15_out), .sel(B[2]));
  Multiplexer multiplexer_16 (.in0(A[3]), .in1(1'b0), .out(multiplexer_16_out), .sel(B[2]));
  Multiplexer multiplexer_17 (.in0(A[4]), .in1(A[0]), .out(multiplexer_17_out), .sel(B[2]));
  Multiplexer multiplexer_18 (.in0(A[5]), .in1(A[1]), .out(multiplexer_18_out), .sel(B[2]));
  Multiplexer multiplexer_19 (.in0(A[6]), .in1(A[2]), .out(multiplexer_19_out), .sel(B[2]));
  Multiplexer multiplexer_20 (.in0(A[7]), .in1(A[3]), .out(multiplexer_20_out), .sel(B[2]));
  not not_11 (not_11_out[0], A[0]);
  not not_12 (not_11_out[1], A[1]);
  not not_13 (not_11_out[2], A[2]);
  not not_14 (not_11_out[3], A[3]);
  not not_15 (not_11_out[4], A[4]);
  not not_16 (not_11_out[5], A[5]);
  not not_17 (not_11_out[6], A[6]);
  not not_18 (not_11_out[7], A[7]);
  xor xor_3 (xor_3_out[0], A[0], B[0]);
  xor xor_4 (xor_3_out[1], A[1], B[1]);
  xor xor_5 (xor_3_out[2], A[2], B[2]);
  xor xor_6 (xor_3_out[3], A[3], B[3]);
  xor xor_7 (xor_3_out[4], A[4], B[4]);
  xor xor_8 (xor_3_out[5], A[5], B[5]);
  xor xor_9 (xor_3_out[6], A[6], B[6]);
  xor xor_10 (xor_3_out[7], A[7], B[7]);
  Multiplexer multiplexer_21 (.in0(multiplexer_5_out), .in1(multiplexer_7_out), .out(multiplexer_21_out), .sel(B[1]));
  Multiplexer multiplexer_22 (.in0(multiplexer_6_out), .in1(multiplexer_8_out), .out(multiplexer_22_out), .sel(B[1]));
  Multiplexer multiplexer_23 (.in0(multiplexer_7_out), .in1(multiplexer_9_out), .out(multiplexer_23_out), .sel(B[1]));
  Multiplexer multiplexer_24 (.in0(multiplexer_8_out), .out(multiplexer_24_out), .sel(B[1]));  // open: in1
  Multiplexer multiplexer_25 (.in0(multiplexer_9_out), .in1(multiplexer_11_out), .out(multiplexer_25_out), .sel(B[1]));
  Multiplexer multiplexer_26 (.in0(multiplexer_10_out), .in1(multiplexer_12_out), .out(multiplexer_26_out), .sel(B[1]));
  Multiplexer multiplexer_27 (.in0(multiplexer_11_out), .in1(1'b0), .out(multiplexer_27_out), .sel(B[1]));
  Multiplexer multiplexer_28 (.in0(multiplexer_12_out), .in1(1'b0), .out(multiplexer_28_out), .sel(B[1]));
  Multiplexer multiplexer_29 (.in0(multiplexer_13_out), .in1(1'b0), .out(multiplexer_29_out), .sel(B[1]));
  Multiplexer multiplexer_30 (.in0(multiplexer_14_out), .in1(1'b0), .out(multiplexer_30_out), .sel(B[1]));
  Multiplexer multiplexer_31 (.in0(multiplexer_15_out), .in1(multiplexer_13_out), .out(multiplexer_31_out), .sel(B[1]));
  Multiplexer multiplexer_32 (.in0(multiplexer_16_out), .in1(multiplexer_14_out), .out(multiplexer_32_out), .sel(B[1]));
  Multiplexer multiplexer_33 (.in0(multiplexer_17_out), .in1(multiplexer_15_out), .out(multiplexer_33_out), .sel(B[1]));
  Multiplexer multiplexer_34 (.in0(multiplexer_18_out), .in1(multiplexer_16_out), .out(multiplexer_34_out), .sel(B[1]));
  Multiplexer multiplexer_35 (.in0(multiplexer_19_out), .in1(multiplexer_17_out), .out(multiplexer_35_out), .sel(B[1]));
  Multiplexer multiplexer_36 (.in0(multiplexer_20_out), .in1(multiplexer_18_out), .out(multiplexer_36_out), .sel(B[1]));
  CLA8 cla8_1 (.A(A), .B(multiplexer_4_out), .Cin(multiplexer_3_out), .C0(C), .Sum(cla8_1_sum));
  Multiplexer multiplexer_37 (
    .in0(multiplexer_21_out), .in1(multiplexer_22_out), .out(multiplexer_37_out[0]), .sel(B[0]));
  Multiplexer multiplexer_38 (
    .in0(multiplexer_22_out), .in1(multiplexer_23_out), .out(multiplexer_37_out[1]), .sel(B[0]));
  Multiplexer multiplexer_39 (
    .in0(multiplexer_23_out), .in1(multiplexer_24_out), .out(multiplexer_37_out[2]), .sel(B[0]));
  Multiplexer multiplexer_40 (
    .in0(multiplexer_24_out), .in1(multiplexer_25_out), .out(multiplexer_37_out[3]), .sel(B[0]));
  Multiplexer multiplexer_41 (
    .in0(multiplexer_25_out), .in1(multiplexer_26_out), .out(multiplexer_37_out[4]), .sel(B[0]));
  Multiplexer multiplexer_42 (
    .in0(multiplexer_26_out), .in1(multiplexer_27_out), .out(multiplexer_37_out[5]), .sel(B[0]));
  Multiplexer multiplexer_43 (
    .in0(multiplexer_27_out), .in1(multiplexer_28_out), .out(multiplexer_37_out[6]), .sel(B[0]));
  Multiplexer multiplexer_44 (.in0(multiplexer_28_out), .in1(1'b0), .out(multiplexer_37_out[7]), .sel(B[0]));
  Multiplexer multiplexer_45 (.in0(multiplexer_29_out), .in1(1'b0), .out(multiplexer_45_out[0]), .sel(B[0]));
  Multiplexer multiplexer_46 (
    .in0(multiplexer_30_out), .in1(multiplexer_29_out), .out(multiplexer_45_out[1]), .sel(B[0]));
  Multiplexer multiplexer_47 (
    .in0(multiplexer_31_out), .in1(multiplexer_30_out), .out(multiplexer_45_out[2]), .sel(B[0]));
  Multiplexer multiplexer_48 (
    .in0(multiplexer_32_out), .in1(multiplexer_31_out), .out(multiplexer_45_out[3]), .sel(B[0]));
  Multiplexer multiplexer_49 (
    .in0(multiplexer_33_out), .in1(multiplexer_32_out), .out(multiplexer_45_out[4]), .sel(B[0]));
  Multiplexer multiplexer_50 (
    .in0(multiplexer_34_out), .in1(multiplexer_33_out), .out(multiplexer_45_out[5]), .sel(B[0]));
  Multiplexer multiplexer_51 (
    .in0(multiplexer_35_out), .in1(multiplexer_34_out), .out(multiplexer_45_out[6]), .sel(B[0]));
  Multiplexer multiplexer_52 (
    .in0(multiplexer_36_out), .in1(multiplexer_35_out), .out(multiplexer_45_out[7]), .sel(B[0]));
  Multiplexer #(.select(3), .width(8)) multiplexer_53 (
    .in0(cla8_1_sum), .in1(cla8_1_sum), .in2(not_11_out), .in3(and_2_out), .in4(xor_3_out), .in5(or_1_out),
    .in6(multiplexer_37_out), .in7(multiplexer_45_out), .out({N, Y[6:0]}), .sel(Opcode));
  // Probe on {N, Y[6:0]}
  // Probe on {N, Y[6:0]}
  // Probe on {N, Y[6:0]}

  assign Y[7] = N;

  // Notes on the sheet:
  //   Status Flags
endmodule

module ProgramCounter (
  input  Cin,
  input  [1:0] Inc,
  input  Load,
  input  Reset,
  input  Clk,
  input  [7:0] Address,
  input  Enable,
  output C,
  output [7:0] PC,
  output [7:0] AlwaysQ
);

  wire [7:0] cla8_1_sum, multiplexer_1_out, register8_1_q;

  CLA8 cla8_1 (.A(register8_1_q), .B({{6{1'b0}}, Inc}), .Cin(Cin), .C0(C), .Sum(cla8_1_sum));
  Multiplexer #(.width(8)) multiplexer_1 (.in0(cla8_1_sum), .in1(Address), .out(multiplexer_1_out), .sel(Load));
  Register8 register8_1 (
    .D(multiplexer_1_out), .Load(1'b1), .Enable(1'b1), .Clk(Clk), .Reset(Reset), .Q(register8_1_q),
    .AlwaysQ(AlwaysQ));
  assign PC = Enable ? register8_1_q : 8'bz;  // Controlled_Buffer controlled_buffer_1
endmodule

module Address_Bus (
  input  [7:0] Address,
  input  Load,
  input  Clk,
  input  Reset,
  input  Cin,
  input  Inc,
  output [7:0] O,
  output Cout
);

  wire [7:0] cla8_1_sum, multiplexer_1_out;

  Multiplexer #(.width(8)) multiplexer_1 (.in0(cla8_1_sum), .in1(Address), .out(multiplexer_1_out), .sel(Load));
  CLA8 cla8_1 (.A(O), .B({{7{1'b0}}, Inc}), .Cin(Cin), .C0(Cout), .Sum(cla8_1_sum));
  Register8 register8_1 (
    .D(multiplexer_1_out), .Load(1'b1), .Enable(1'b1), .Clk(Clk), .Reset(Reset), .Q(O));  // open: AlwaysQ
endmodule

module Increment8 (
  input  Reset,
  input  Clk,
  input  Cin,
  input  Inc,
  output [7:0] O
);

  wire [7:0] cla8_1_sum;

  CLA8 cla8_1 (.A(O), .B({{7{1'b0}}, Inc}), .Cin(Cin), .Sum(cla8_1_sum));  // open: C0
  Register8 register8_1 (.D(cla8_1_sum), .Load(1'b1), .Enable(1'b1), .Clk(Clk), .Reset(Reset), .Q(O));  // open: AlwaysQ
endmodule

module Increment4 (
  input  Reset,
  input  Clk,
  output [3:0] O
);

  wire d_flipflop_1_q, undriven;
  wire [3:0] cla4_1_sum;

  D_FlipFlop d_flipflop_1 (.D(Reset), .Clk(Clk), .Reset(undriven), .Q(d_flipflop_1_q));  // open: Qbar
  CLA4 cla4_1 (.A(O), .B(4'b0001), .Sum(cla4_1_sum));  // open: Cin, Cout, PG, GG
  D_FlipFlop d_flipflop_2 (.D(cla4_1_sum[0]), .Clk(Clk), .Reset(d_flipflop_1_q), .Q(O[0]));  // open: Qbar
  D_FlipFlop d_flipflop_3 (.D(cla4_1_sum[1]), .Clk(Clk), .Reset(d_flipflop_1_q), .Q(O[1]));  // open: Qbar
  D_FlipFlop d_flipflop_4 (.D(cla4_1_sum[2]), .Clk(Clk), .Reset(d_flipflop_1_q), .Q(O[2]));  // open: Qbar
  D_FlipFlop d_flipflop_5 (.D(cla4_1_sum[3]), .Clk(Clk), .Reset(d_flipflop_1_q), .Q(O[3]));  // open: Qbar
endmodule

module Register8 (
  input  [7:0] D,
  input  Load,
  input  Enable,
  input  Clk,
  input  Reset,
  output [7:0] Q,
  output [7:0] AlwaysQ
);

  wire multiplexer_1_out, multiplexer_2_out, multiplexer_3_out, multiplexer_4_out, multiplexer_5_out,
       multiplexer_6_out, multiplexer_7_out, multiplexer_8_out;

  Multiplexer multiplexer_1 (.in0(AlwaysQ[0]), .in1(D[0]), .out(multiplexer_1_out), .sel(Load));
  Multiplexer multiplexer_2 (.in0(AlwaysQ[1]), .in1(D[1]), .out(multiplexer_2_out), .sel(Load));
  Multiplexer multiplexer_3 (.in0(AlwaysQ[2]), .in1(D[2]), .out(multiplexer_3_out), .sel(Load));
  Multiplexer multiplexer_4 (.in0(AlwaysQ[3]), .in1(D[3]), .out(multiplexer_4_out), .sel(Load));
  Multiplexer multiplexer_5 (.in0(AlwaysQ[4]), .in1(D[4]), .out(multiplexer_5_out), .sel(Load));
  Multiplexer multiplexer_6 (.in0(AlwaysQ[5]), .in1(D[5]), .out(multiplexer_6_out), .sel(Load));
  Multiplexer multiplexer_7 (.in0(AlwaysQ[6]), .in1(D[6]), .out(multiplexer_7_out), .sel(Load));
  Multiplexer multiplexer_8 (.in0(AlwaysQ[7]), .in1(D[7]), .out(multiplexer_8_out), .sel(Load));
  D_FlipFlop d_flipflop_1 (.D(multiplexer_1_out), .Clk(Clk), .Reset(Reset), .Q(AlwaysQ[0]));  // open: Qbar
  D_FlipFlop d_flipflop_2 (.D(multiplexer_2_out), .Clk(Clk), .Reset(Reset), .Q(AlwaysQ[1]));  // open: Qbar
  D_FlipFlop d_flipflop_3 (.D(multiplexer_3_out), .Clk(Clk), .Reset(Reset), .Q(AlwaysQ[2]));  // open: Qbar
  D_FlipFlop d_flipflop_4 (.D(multiplexer_4_out), .Clk(Clk), .Reset(Reset), .Q(AlwaysQ[3]));  // open: Qbar
  D_FlipFlop d_flipflop_5 (.D(multiplexer_5_out), .Clk(Clk), .Reset(Reset), .Q(AlwaysQ[4]));  // open: Qbar
  D_FlipFlop d_flipflop_6 (.D(multiplexer_6_out), .Clk(Clk), .Reset(Reset), .Q(AlwaysQ[5]));  // open: Qbar
  D_FlipFlop d_flipflop_7 (.D(multiplexer_7_out), .Clk(Clk), .Reset(Reset), .Q(AlwaysQ[6]));  // open: Qbar
  D_FlipFlop d_flipflop_8 (.D(multiplexer_8_out), .Clk(Clk), .Reset(Reset), .Q(AlwaysQ[7]));  // open: Qbar
  assign Q = Enable ? AlwaysQ : 8'bz;  // Controlled_Buffer controlled_buffer_1
endmodule

module DataLatch8 (
  input  [7:0] D,
  input  Load,
  input  Enable,
  output [7:0] Q,
  output [7:0] AlwaysQ
);

  D_Latch d_latch_1 (.D(D[0]), .Enable(Load), .Q(AlwaysQ[0]));  // open: Qbar
  D_Latch d_latch_2 (.D(D[1]), .Enable(Load), .Q(AlwaysQ[1]));  // open: Qbar
  D_Latch d_latch_3 (.D(D[2]), .Enable(Load), .Q(AlwaysQ[2]));  // open: Qbar
  D_Latch d_latch_4 (.D(D[3]), .Enable(Load), .Q(AlwaysQ[3]));  // open: Qbar
  D_Latch d_latch_5 (.D(D[4]), .Enable(Load), .Q(AlwaysQ[4]));  // open: Qbar
  D_Latch d_latch_6 (.D(D[5]), .Enable(Load), .Q(AlwaysQ[5]));  // open: Qbar
  D_Latch d_latch_7 (.D(D[6]), .Enable(Load), .Q(AlwaysQ[6]));  // open: Qbar
  D_Latch d_latch_8 (.D(D[7]), .Enable(Load), .Q(AlwaysQ[7]));  // open: Qbar
  assign Q = Enable ? AlwaysQ : 8'bz;  // Controlled_Buffer controlled_buffer_1
endmodule

module Register4 (
  input  [3:0] D,
  input  Load,
  input  Enable,
  input  Clk,
  input  Reset,
  output [3:0] Q,
  output [3:0] AlwaysQ
);

  wire multiplexer_1_out, multiplexer_2_out, multiplexer_3_out, multiplexer_4_out;

  Multiplexer multiplexer_1 (.in0(AlwaysQ[0]), .in1(D[0]), .out(multiplexer_1_out), .sel(Load));
  Multiplexer multiplexer_2 (.in0(AlwaysQ[1]), .in1(D[1]), .out(multiplexer_2_out), .sel(Load));
  Multiplexer multiplexer_3 (.in0(AlwaysQ[2]), .in1(D[2]), .out(multiplexer_3_out), .sel(Load));
  Multiplexer multiplexer_4 (.in0(AlwaysQ[3]), .in1(D[3]), .out(multiplexer_4_out), .sel(Load));
  D_FlipFlop d_flipflop_1 (.D(multiplexer_1_out), .Clk(Clk), .Reset(Reset), .Q(AlwaysQ[0]));  // open: Qbar
  D_FlipFlop d_flipflop_2 (.D(multiplexer_2_out), .Clk(Clk), .Reset(Reset), .Q(AlwaysQ[1]));  // open: Qbar
  D_FlipFlop d_flipflop_3 (.D(multiplexer_3_out), .Clk(Clk), .Reset(Reset), .Q(AlwaysQ[2]));  // open: Qbar
  D_FlipFlop d_flipflop_4 (.D(multiplexer_4_out), .Clk(Clk), .Reset(Reset), .Q(AlwaysQ[3]));  // open: Qbar
  assign Q = Enable ? AlwaysQ : 4'bz;  // Controlled_Buffer controlled_buffer_1
endmodule

module StackRegister8 (
  input  [7:0] D,
  input  Load,
  input  Enable,
  input  Clk,
  input  Reset,
  output [7:0] Q,
  output [7:0] AlwaysQ
);

  wire multiplexer_1_out, multiplexer_2_out, multiplexer_3_out, multiplexer_4_out, multiplexer_5_out,
       multiplexer_6_out, multiplexer_7_out, multiplexer_8_out, multiplexer_9_out, multiplexer_10_out,
       multiplexer_11_out, multiplexer_12_out, multiplexer_13_out, multiplexer_14_out, multiplexer_15_out,
       multiplexer_16_out;

  Multiplexer multiplexer_1 (.in0(AlwaysQ[0]), .in1(D[0]), .out(multiplexer_1_out), .sel(Load));
  Multiplexer multiplexer_2 (.in0(AlwaysQ[1]), .in1(D[1]), .out(multiplexer_2_out), .sel(Load));
  Multiplexer multiplexer_3 (.in0(AlwaysQ[2]), .in1(D[2]), .out(multiplexer_3_out), .sel(Load));
  Multiplexer multiplexer_4 (.in0(AlwaysQ[3]), .in1(D[3]), .out(multiplexer_4_out), .sel(Load));
  Multiplexer multiplexer_5 (.in0(AlwaysQ[4]), .in1(D[4]), .out(multiplexer_5_out), .sel(Load));
  Multiplexer multiplexer_6 (.in0(AlwaysQ[5]), .in1(D[5]), .out(multiplexer_6_out), .sel(Load));
  Multiplexer multiplexer_7 (.in0(AlwaysQ[6]), .in1(D[6]), .out(multiplexer_7_out), .sel(Load));
  Multiplexer multiplexer_8 (.in0(AlwaysQ[7]), .in1(D[7]), .out(multiplexer_8_out), .sel(Load));
  Multiplexer multiplexer_9 (.in0(multiplexer_1_out), .in1(1'b1), .out(multiplexer_9_out), .sel(Reset));
  Multiplexer multiplexer_10 (.in0(multiplexer_2_out), .in1(1'b1), .out(multiplexer_10_out), .sel(Reset));
  Multiplexer multiplexer_11 (.in0(multiplexer_3_out), .in1(1'b1), .out(multiplexer_11_out), .sel(Reset));
  Multiplexer multiplexer_12 (.in0(multiplexer_4_out), .in1(1'b1), .out(multiplexer_12_out), .sel(Reset));
  Multiplexer multiplexer_13 (.in0(multiplexer_5_out), .in1(1'b1), .out(multiplexer_13_out), .sel(Reset));
  Multiplexer multiplexer_14 (.in0(multiplexer_6_out), .in1(1'b1), .out(multiplexer_14_out), .sel(Reset));
  Multiplexer multiplexer_15 (.in0(multiplexer_7_out), .in1(1'b1), .out(multiplexer_15_out), .sel(Reset));
  Multiplexer multiplexer_16 (.in0(multiplexer_8_out), .in1(1'b1), .out(multiplexer_16_out), .sel(Reset));
  D_FlipFlop d_flipflop_1 (.D(multiplexer_9_out), .Clk(Clk), .Q(AlwaysQ[0]));  // open: Reset, Qbar
  D_FlipFlop d_flipflop_2 (.D(multiplexer_10_out), .Clk(Clk), .Q(AlwaysQ[1]));  // open: Reset, Qbar
  D_FlipFlop d_flipflop_3 (.D(multiplexer_11_out), .Clk(Clk), .Q(AlwaysQ[2]));  // open: Reset, Qbar
  D_FlipFlop d_flipflop_4 (.D(multiplexer_12_out), .Clk(Clk), .Q(AlwaysQ[3]));  // open: Reset, Qbar
  D_FlipFlop d_flipflop_5 (.D(multiplexer_13_out), .Clk(Clk), .Q(AlwaysQ[4]));  // open: Reset, Qbar
  D_FlipFlop d_flipflop_6 (.D(multiplexer_14_out), .Clk(Clk), .Q(AlwaysQ[5]));  // open: Reset, Qbar
  D_FlipFlop d_flipflop_7 (.D(multiplexer_15_out), .Clk(Clk), .Q(AlwaysQ[6]));  // open: Reset, Qbar
  D_FlipFlop d_flipflop_8 (.D(multiplexer_16_out), .Clk(Clk), .Q(AlwaysQ[7]));  // open: Reset, Qbar
  assign Q = Enable ? AlwaysQ : 8'bz;  // Controlled_Buffer controlled_buffer_1
endmodule

module Negate8 (
  input  [7:0] A,
  output [7:0] NegA
);

  wire [7:0] not_1_out;

  // Probe on A
  not not_1 (not_1_out[0], A[0]);
  not not_2 (not_1_out[1], A[1]);
  not not_3 (not_1_out[2], A[2]);
  not not_4 (not_1_out[3], A[3]);
  not not_5 (not_1_out[4], A[4]);
  not not_6 (not_1_out[5], A[5]);
  not not_7 (not_1_out[6], A[6]);
  not not_8 (not_1_out[7], A[7]);
  CLA8 cla8_1 (.A(not_1_out), .B(8'h1), .Sum(NegA));  // open: Cin, C0
  // Probe on NegA
endmodule

module CLA8 (
  input  [7:0] A,
  input  [7:0] B,
  input  Cin,
  output C0,
  output [7:0] Sum
);

  wire cla4_1_gg, cla4_1_pg, cla4_2_gg, cla4_2_pg, lcu2_1_c1;

  // Probe on A
  // Probe on B
  CLA4 cla4_1 (.A(A[7:4]), .B(B[7:4]), .Cin(lcu2_1_c1), .Sum(Sum[7:4]), .PG(cla4_1_pg), .GG(cla4_1_gg));  // open: Cout
  CLA4 cla4_2 (.A(A[3:0]), .B(B[3:0]), .Cin(Cin), .Sum(Sum[3:0]), .PG(cla4_2_pg), .GG(cla4_2_gg));  // open: Cout
  LCU2 lcu2_1 (.P1(cla4_1_pg), .G1(cla4_1_gg), .P0(cla4_2_pg), .G0(cla4_2_gg), .C0(Cin), .C2(C0), .C1(lcu2_1_c1));
  // Probe on Sum
endmodule

module CLA4 (
  input  [3:0] A,
  input  [3:0] B,
  input  Cin,
  output Cout,
  output [3:0] Sum,
  output PG,
  output GG
);

  wire partialfulladder_1_g, partialfulladder_1_p, partialfulladder_2_g, partialfulladder_2_p,
       partialfulladder_3_g, partialfulladder_3_p, partialfulladder_4_g, partialfulladder_4_p;

  PartialFullAdder partialfulladder_1 (.A(A[3]), .B(B[3]), .P(partialfulladder_1_p), .G(partialfulladder_1_g));
  PartialFullAdder partialfulladder_2 (.A(A[2]), .B(B[2]), .P(partialfulladder_2_p), .G(partialfulladder_2_g));
  PartialFullAdder partialfulladder_3 (.A(A[1]), .B(B[1]), .P(partialfulladder_3_p), .G(partialfulladder_3_g));
  PartialFullAdder partialfulladder_4 (.A(A[0]), .B(B[0]), .P(partialfulladder_4_p), .G(partialfulladder_4_g));
  CLU4 clu4_1 (
    .P3(partialfulladder_1_p), .G3(partialfulladder_1_g), .P2(partialfulladder_2_p),
    .G2(partialfulladder_2_g), .P1(partialfulladder_3_p), .G1(partialfulladder_3_g),
    .P0(partialfulladder_4_p), .G0(partialfulladder_4_g), .C0(Cin), .PG(PG), .GG(GG), .C4(Cout), .S3(Sum[3]),
    .S2(Sum[2]), .S1(Sum[1]), .S0(Sum[0]));
  // Probe on Sum
endmodule

module PartialFullAdder (
  input  A,
  input  B,
  output P,
  output G
);

  and and_1 (G, A, B);
  xor xor_1 (P, A, B);
endmodule

module CLU4 (
  input  P3,
  input  G3,
  input  P2,
  input  G2,
  input  P1,
  input  G1,
  input  P0,
  input  G0,
  input  C0,
  output PG,
  output GG,
  output C4,
  output S3,
  output S2,
  output S1,
  output S0
);

  wire and_1_out, and_2_out, and_3_out, and_4_out, and_5_out, and_6_out, and_7_out, and_8_out, and_9_out,
       and_10_out, or_1_out, or_2_out, or_3_out;

  and and_1 (and_1_out, P3, P2, P1, P0, C0);
  and and_2 (and_2_out, P3, P2, P1, G0);
  and and_3 (and_3_out, P3, P2, G1);
  and and_4 (and_4_out, G2, P3);
  and and_5 (and_5_out, P2, P1, P0, C0);
  and and_6 (and_6_out, P2, P1, G0);
  and and_7 (and_7_out, G1, P2);
  and and_8 (and_8_out, P1, P0, C0);
  and and_9 (and_9_out, G0, P1);
  and and_10 (and_10_out, C0, P0);
  or or_1 (or_1_out, and_5_out, and_6_out, and_7_out, G2);
  or or_2 (or_2_out, and_8_out, and_9_out, G1);
  or or_3 (or_3_out, and_10_out, G0);
  and and_11 (PG, P3, P2, P1, P0);
  or or_4 (GG, and_2_out, and_3_out, and_4_out, G3);
  or or_5 (C4, and_1_out, and_2_out, and_3_out, and_4_out, G3);
  xor xor_1 (S3, P3, or_1_out);
  xor xor_2 (S2, P2, or_2_out);
  xor xor_3 (S1, P1, or_3_out);
  xor xor_4 (S0, P0, C0);
endmodule

module LCU2 (
  input  P1,
  input  G1,
  input  P0,
  input  G0,
  input  C0,
  output C2,
  output C1
);

  wire and_1_out, and_2_out, and_3_out;

  and and_1 (and_1_out, P1, P0, C0);
  and and_2 (and_2_out, G0, P1);
  and and_3 (and_3_out, C0, P0);
  or or_1 (C2, and_1_out, and_2_out, G1);
  or or_2 (C1, and_3_out, G0);
endmodule

module D_FlipFlop (
  input  D,
  input  Clk,
  input  Reset,
  output Q,
  output Qbar
);

  wire nand_1_out, nand_2_out, nand_3_out, nand_4_out, not_1_out;

  not not_1 (not_1_out, Reset);
  nand nand_1 (nand_1_out, nand_4_out, nand_2_out);
  nand nand_2 (nand_2_out, nand_1_out, Clk, not_1_out);
  nand nand_3 (nand_3_out, nand_2_out, Clk, nand_4_out);
  nand nand_4 (nand_4_out, nand_3_out, D, not_1_out);
  nand nand_5 (Q, nand_2_out, Qbar);
  nand nand_6 (Qbar, Q, nand_3_out, not_1_out);
endmodule

module D_Latch (
  input  D,
  input  Enable,
  output Q,
  output Qbar
);

  wire nand_1_out, nand_2_out, not_1_out;

  not not_1 (not_1_out, D);
  nand nand_1 (nand_1_out, D, Enable);
  nand nand_2 (nand_2_out, Enable, not_1_out);
  nand nand_3 (Q, nand_1_out, Qbar);
  nand nand_4 (Qbar, Q, nand_2_out);
endmodule
